// Logisim project CPU.circ as structural Verilog: 1 circuit, main circuit main
module main (
);

  wire main_1_alusrc, main_1_exop, main_1_memread, main_1_memtoreg, main_1_memwrite, main_1_regdes,
       main_1_regwrite;
  wire [4:0] multiplexer_1_out, PC_q, undriven;
  wire [31:0] main_2_rs_output, main_2_rt_output, main_3_result, main_4_p3, multiplexer_2_out,
       multiplexer_3_out, ram_1_data, ram_2_data;

  Register #(.width(5)) PC (.D(undriven), .Q(PC_q));  // open: en, clk, clr
  RAM #(.addrWidth(5), .dataWidth(32), .bus("separate")) ram_1 (
    .addr(PC_q), .data(ram_1_data));  // open: din, str, sel, clk, ld, clr
  Control_Unit_main main_1 (
    .OP_Code(ram_1_data[31:26]), .RegDes(main_1_regdes), .ALUsrc(main_1_alusrc), .RegWrite(main_1_regwrite),
    .MemWrite(main_1_memwrite), .MemRead(main_1_memread), .MemToReg(main_1_memtoreg), .ExOp(main_1_exop));  // open: jump, branch
  Multiplexer #(.width(5), .enable("false")) multiplexer_1 (
    .in0(ram_1_data[20:16]), .in1(ram_1_data[15:11]), .out(multiplexer_1_out), .sel(main_1_regdes));
  Register_File_main main_2 (
    .Rs_Output(main_2_rs_output), .Rt_Output(main_2_rt_output), .Rs(ram_1_data[25:21]),
    .Rt(ram_1_data[20:16]), .Reg_Write(main_1_regwrite), .Rd(multiplexer_1_out),
    .Write_Data(multiplexer_3_out));  // open: Clock
  Extension_Unit_main main_3 (.\input (ram_1_data[15:0]), .Result(main_3_result), .ExOp(main_1_exop));
  Multiplexer #(.width(32), .enable("false")) multiplexer_2 (
    .in0(main_2_rt_output), .in1(main_3_result), .out(multiplexer_2_out), .sel(main_1_alusrc));
  // ALU_main main_4: pin names not known; wires that end beside it: main_2_rs_output, multiplexer_2_out, main_4_p3, main_4_p3[4:0]
  RAM #(.addrWidth(5), .dataWidth(32), .bus("separate")) ram_2 (
    .addr(main_4_p3[4:0]), .din(main_2_rt_output), .data(ram_2_data), .str(main_1_memwrite),
    .ld(main_1_memread));  // open: sel, clk, clr
  Multiplexer #(.width(32), .enable("false")) multiplexer_3 (
    .in0(main_4_p3), .in1(ram_2_data), .out(multiplexer_3_out), .sel(main_1_memtoreg));
endmodule
